// Logisim project X0_Isa.circ as structural Verilog: 1 circuit, main circuit main
module main (
  input  A,
  input  B,
  input  C,
  input  D,
  output X
);

  wire and_1_out, and_2_out, and_3_out, and_4_out, and_5_out, not_1_out, not_2_out;

  not not_1 (not_1_out, C);
  not not_2 (not_2_out, D);
  and and_1 (and_1_out, A, B);
  and and_2 (and_2_out, A, not_1_out);
  and and_3 (and_3_out, not_1_out, B);
  and and_4 (and_4_out, A, not_2_out);
  and and_5 (and_5_out, not_1_out, not_2_out);
  or or_1 (X, and_1_out, and_2_out, and_3_out, and_4_out, and_5_out);
endmodule
