// Logisim project X2_Isa.circ as structural Verilog: 1 circuit, main circuit main
module main (
  input  A,
  input  B,
  input  C,
  input  D,
  output X
);

  wire and_1_out, and_2_out, and_3_out, not_1_out, not_2_out;

  not not_1 (not_1_out, A);
  not not_2 (not_2_out, B);
  and and_1 (and_1_out, not_1_out, C);
  and and_2 (and_2_out, not_2_out, C, D);
  and and_3 (and_3_out, not_1_out, not_2_out, D);
  or or_1 (X, and_1_out, and_2_out, and_3_out);
endmodule
